# Fritzing sketch moving_servor_motor (saved by Fritzing 0.9.3b)

parts:
  부품1 = Arduino Uno (Rev3)
  J1 = Basic Servo

nets:
  N1: 부품1.D9_PWM, J1.pulse
  5V: 부품1.5V, J1.vcc
  GND: 부품1.GND, J1.gnd

notes:
  터보의 빨간색(+)은 5v로 연결
  파란색 선(보통 갈색)은 gnd로 연결
  노란색 선은 디지털 9번 핀으로 연결
