# Fritzing sketch toneMelody (saved by Fritzing 0.9.3b)

parts:
  J1 = Piezo Speaker
  부품1 = Arduino Uno (Rev3)

nets:
  N1: J1.pin1, 부품1.GND
  N2: J1.pin2, 부품1.D8

notes:
  검은색 선은 gnd로
  빨간색 선은 디지털 8번 핀으
