# Fritzing sketch rgb_led (saved by Fritzing 0.9.3b)
breadboards: 1

parts:
  부품1 = Arduino Uno (Rev3)
  LED1 = RGB LED (com. cathode, rbg) [package="5 mm [THT]"]
  R1 = Resistor [tolerance=±5% resistance=220 package=THT]
  R2 = Resistor [tolerance=±5% resistance=220 package=THT]
  R3 = Resistor [tolerance=±5% resistance=220 package=THT]

nets:
  N1: 부품1.D9_PWM, R3.Pin_1
  N2: 부품1.D10_PWM/SS, R2.Pin_1
  N3: 부품1.D11_PWM/MOSI, R1.Pin_1
  N4: 부품1.GND, LED1.common_cathode
  N5: LED1.red_anode, R1.Pin_0
  N6: LED1.blue_anode, R2.Pin_0
  N7: LED1.green_anode, R3.Pin_0

notes:
  rgb led 이용하기
  1. 왼쪽에서 두번째 제일 긴 다리 -> gnd
  2. 왼쪽에서 첫번째 -> digital 11 pin
  3. 왼쪽에서 세번째 -> digital 10 pin
  4. 맨 오른쪽 다리 -> digital 9 pin
  우리가 이용하는 rgb led는 common cathode type
  즉 세개의 led들의 (-)들을 묶은 것
  HIGH로 켠다.
