# Fritzing sketch ultrasonic_example (saved by Fritzing 0.9.3b)
breadboards: 1

parts:
  부품1 = Arduino Uno (Rev3)
  hc-sr1 = hc-sr04

nets:
  N1: 부품1.D2, hc-sr1.Trig
  N2: 부품1.D3_PWM, hc-sr1.GND
  5V: 부품1.5V, hc-sr1.VCC

notes:
  초음파 센서 이용하기
  1. vcc -> 5v
  2. gnd -> gnd
  3. trig -> digital 2 pin
  4. echo -> digital 3 pin
